# Fritzing sketch schematic (saved by Fritzing 0.9.3b)
breadboards: 1

parts:
  AM1 = AM2302 Humidity and Temperature Sensor
  Display = OLED Monochrome 128x64 1.3 inch [part_number=938]
  U1 = RELAY-SOLIDSTATE [package=relay-s108t02]
  Trinket = Adafruit Trinket M0 [part_number="Adafruit #3500"]
  LM1 = RioRand LM2596

nets:
  VDD: AM1.VDD, Display.VIN, Trinket.VBAT, LM1.Pin_2
  N1: AM1.DATA, Trinket.D4_A2_PA06_TXD_MOSI
  GND: AM1.GND, Display.GND, U1.+, Trinket.GND, LM1.Pin_3
  N2: Display.MOSI_SDA, Trinket.D0_A4_PA08_SDA
  N3: Display.SCLK_SCK, Trinket.D2_A1_PA09_SCL_MISO
  N4: Display.RESET, Trinket.D1_A0_PA02
  N5: U1.-, Trinket.D3_A3_PA07_RXD_SCK

custom parts:
  OLED Monochrome 128x64 1.3 inch: These displays are small, only about 1.3" diagonal, but very readable due to the high contrast of an OLED display. This display is made of 128x64 individual white OLED pixels, each one is turned on or off by the controller chip. Because the display makes its own light, no backlight is required. This reduces the power required to run the OLED and is why the display has such high contrast; we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
